// Logisim project ASC-1.circ as structural Verilog: 16 circuits, main circuit main
module main (
);

  wire button_1_out, button_2_out, clockgenerator_1_out_4, controlunit_1_out_5, controlunit_1_out_6,
       controlunit_1_out_8, controlunit_1_out_9, controlunit_1_out_10, controlunit_1_out_11,
       controlunit_1_out_12, controlunit_1_out_13, controlunit_1_out_14, controlunit_1_out_15,
       controlunit_1_out_16, controlunit_1_out_17, controlunit_1_out_18, controlunit_1_out_19,
       controlunit_1_out_20, controlunit_1_out_21, or_1_out, por_1_out, RESET_out;
  wire [3:0] alu_1_out_8, controlunit_1_out_7;
  wire [7:0] hardwarestack_1_out_6, instructionregister_1_out_8, memoryaddressregister_1_out_5,
       ram_256b_1_out_7, register_a_1_out_7, register_b_1_out_7;

  Button RESET (.out(RESET_out));
  Button button_1 (.out(button_1_out));
  Button button_2 (.out(button_2_out));
  HardwareStack hardwarestack_1 (
    .RST(or_1_out), .CLK(clockgenerator_1_out_4), .Push(controlunit_1_out_17), .Pop(controlunit_1_out_18),
    .in_5(hardwarestack_1_out_6), .out_6(hardwarestack_1_out_6));
  POR por_1 (.out(por_1_out));
  ControlUnit controlunit_1 (
    .in_4(instructionregister_1_out_8), .in_3(alu_1_out_8), .in_1(clockgenerator_1_out_4), .in_2(or_1_out),
    .out_7(controlunit_1_out_7), .out_5(controlunit_1_out_5), .out_6(controlunit_1_out_6),
    .out_8(controlunit_1_out_8), .out_9(controlunit_1_out_9), .out_10(controlunit_1_out_10),
    .out_11(controlunit_1_out_11), .out_12(controlunit_1_out_12), .out_13(controlunit_1_out_13),
    .out_14(controlunit_1_out_14), .out_15(controlunit_1_out_15), .out_16(controlunit_1_out_16),
    .out_17(controlunit_1_out_17), .out_18(controlunit_1_out_18), .out_19(controlunit_1_out_19),
    .out_20(controlunit_1_out_20), .out_21(controlunit_1_out_21));
  or or_1 (or_1_out, por_1_out, RESET_out);
  // Probe on hardwarestack_1_out_6
  ClockGenerator clockgenerator_1 (
    .in_1(button_1_out), .in_3(controlunit_1_out_21), .in_2(button_2_out), .out_4(clockgenerator_1_out_4));  // open: out_5
  MemoryAddressRegister memoryaddressregister_1 (
    .in_1(hardwarestack_1_out_6), .in_2(controlunit_1_out_14), .in_3(clockgenerator_1_out_4),
    .in_4(or_1_out), .out_5(memoryaddressregister_1_out_5));
  RAM_256B ram_256b_1 (
    .in_1(memoryaddressregister_1_out_5), .in_2(controlunit_1_out_15), .CLK(clockgenerator_1_out_4),
    .in_5(hardwarestack_1_out_6), .in_3(controlunit_1_out_16), .out_7(ram_256b_1_out_7),
    .out_6(hardwarestack_1_out_6));
  InstructionRegister instructionregister_1 (
    .in_1(ram_256b_1_out_7), .in_2(hardwarestack_1_out_6), .in_3(controlunit_1_out_19),
    .in_4(clockgenerator_1_out_4), .in_5(or_1_out), .out_7(hardwarestack_1_out_6),
    .out_8(instructionregister_1_out_8));  // open: in_6
  PC pc_1 (
    .CLR(or_1_out), .STR(controlunit_1_out_5), .CE(controlunit_1_out_8), .CLK(clockgenerator_1_out_4),
    .CO(controlunit_1_out_6), .in_5(hardwarestack_1_out_6), .out_7(hardwarestack_1_out_6));
  Register_A register_a_1 (
    .in_1(hardwarestack_1_out_6), .in_2(controlunit_1_out_9), .in_3(clockgenerator_1_out_4), .in_4(or_1_out),
    .in_5(controlunit_1_out_10), .out_6(hardwarestack_1_out_6), .out_7(register_a_1_out_7));
  Register_B register_b_1 (
    .in_1(hardwarestack_1_out_6), .in_2(controlunit_1_out_11), .in_3(clockgenerator_1_out_4),
    .in_4(or_1_out), .in_5(controlunit_1_out_12), .out_6(hardwarestack_1_out_6), .out_7(register_b_1_out_7));
  OutReg outreg_1 (
    .in_1(hardwarestack_1_out_6), .in_2(controlunit_1_out_20), .in_3(clockgenerator_1_out_4), .in_4(or_1_out));
  ALU alu_1 (
    .A(register_a_1_out_7), .B(register_b_1_out_7), .in_5(clockgenerator_1_out_4), .in_6(or_1_out),
    .in_4(controlunit_1_out_13), .in_1(controlunit_1_out_7), .out_7(hardwarestack_1_out_6),
    .out_8(alu_1_out_8));
endmodule

module ClockGenerator (
  input  in_1,
  input  in_2,
  input  in_3,
  output out_4,
  output out_5
);

  wire and_1_out, clock_1_out, not_1_out, or_1_out, t_ff_1_q, t_ff_1_qn;

  T_Flip_Flop t_ff_1 (.T(1'b1), .clk(in_2), .Q(t_ff_1_q), .Qn(t_ff_1_qn));  // open: reset, preset
  not not_1 (not_1_out, t_ff_1_qn);
  LED led_1 (.in(not_1_out));
  Clock clock_1 (.out(clock_1_out));
  and and_1 (and_1_out, clock_1_out, ~t_ff_1_q);  // AND_Gate
  or or_1 (or_1_out, and_1_out, in_1);
  and and_2 (out_4, or_1_out, ~in_3);  // AND_Gate
  LED led_2 (.in(in_3));
  LED led_3 (.in(out_4));
  not not_2 (out_5, out_4);
endmodule

module ControlUnit (
  input  in_1,
  input  in_2,
  input  [3:0] in_3,
  input  [7:0] in_4,
  output out_5,
  output out_6,
  output [3:0] out_7,
  output out_8,
  output out_9,
  output out_10,
  output out_11,
  output out_12,
  output out_13,
  output out_14,
  output out_15,
  output out_16,
  output out_17,
  output out_18,
  output out_19,
  output out_20,
  output out_21
);

  wire [1:0] counter_1_q;

  Counter #(.max('h3), .trigger("falling"), .width(2)) counter_1 (
    .clr(in_2), .clk(in_1), .Q(counter_1_q));  // open: load, up, count, D, carry
  // Probe on {in_4[3:0], in_3, counter_1_q}
  ROM #(.addrWidth(10), .dataWidth(16)) rom_1 (
    .addr({in_4[3:0], in_3, counter_1_q}),
    .data({out_21, out_20, out_19, out_18, out_17, out_16, out_15, out_14, out_13, out_12, out_11, out_10, out_9, out_8, out_6, out_5}));

  assign out_7 = in_4[7:4];

  // Notes on the sheet:
  //   contents of rom_1 (hex, n*v repeats v):
  //   4 0 0 102 4 0 0 102 4 0 0 102 4 0 0 102 4 0 0 102 4 0 0 102 4 0 0 102 4 0 0 102 4 0 0 102 4 0 0 102
  //   4 0 0 102 4 0 0 102 4 0 0 102 4 0 0 102 4 0 0 102 4 0 0 102 4 500 408 102 4 500 408 102 4 500 408
  //   102 4 500 408 102 4 500 408 102 4 500 408 102 4 500 408 102 4 500 408 102 4 500 408 102 4 500 408
  //   102 4 500 408 102 4 500 408 102 4 500 408 102 4 500 408 102 4 500 408 102 4 500 408 102 4 500 420
  //   102 4 500 420 102 4 500 420 102 4 500 420 102 4 500 420 102 4 500 420 102 4 500 420 102 4 500 420
  //   102 4 500 420 102 4 500 420 102 4 500 420 102 4 500 420 102 4 500 420 102 4 500 420 102 4 500 420
  //   102 4 500 420 102 4 408 0 102 4 408 0 102 4 408 0 102 4 408 0 102 4 408 0 102 4 408 0 102 4 408 0
  //   102 4 408 0 102 4 408 0 102 4 408 0 102 4 408 0 102 4 408 0 102 4 408 0 102 4 408 0 102 4 408 0 102
  //   4 408 0 102 4 500 210 102 4 500 210 102 4 500 210 102 4 500 210 102 4 500 210 102 4 500 210 102 4
  //   500 210 102 4 500 210 102 4 500 210 102 4 500 210 102 4 500 210 102 4 500 210 102 4 500 210 102 4
  //   500 210 102 4 500 210 102 4 500 210 102 4 500 240 102 4 500 240 102 4 500 240 102 4 500 240 102 4
  //   500 240 102 4 500 240 102 4 500 240 102 4 500 240 102 4 500 240 102 4 500 240 102 4 500 240 102 4
  //   500 240 102 4 500 240 102 4 500 240 102 4 500 240 102 4 500 240 102 4 401 0 102 4 401 0 102 4 401 0
  //   102 4 401 0 102 4 401 0 102 4 401 0 102 4 401 0 102 4 401 0 102 4 401 0 102 4 401 0 102 4 401 0 102
  //   4 401 0 102 4 401 0 102 4 401 0 102 4 401 0 102 4 401 0 102 4 0 0 102 4 401 0 102 4 0 0 102 4 401 0
  //   102 4 0 0 102 4 401 0 102 4 0 0 102 4 401 0 102 4 0 0 102 4 401 0 102 4 0 0 102 4 401 0 102 4 0 0
  //   102 4 401 0 102 4 0 0 102 4 401 0 102 4 0 0 102 4 0 0 102 4 401 0 102 4 401 0 102 4 0 0 102 4 0 0
  //   102 4 401 0 102 4 401 0 102 4 0 0 102 4 0 0 102 4 401 0 102 4 401 0 102 4 0 0 102 4 0 0 102 4 401 0
  //   102 4 401 0 102 4 0 0 102 4 0 0 102 4 0 0 102 4 0 0 102 4 401 0 102 4 401 0 102 4 401 0 102 4 401 0
  //   102 4 0 0 102 4 0 0 102 4 0 0 102 4 0 0 102 4 401 0 102 4 401 0 102 4 401 0 102 4 401 0 102 4 0 0
  //   102 4 0 0 102 4 0 0 102 4 0 0 102 4 0 0 102 4 0 0 102 4 0 0 102 4 0 0 102 4 401 0 102 4 401 0 102 4
  //   401 0 102 4 401 0 102 4 401 0 102 4 401 0 102 4 401 0 102 4 401 0 102 4 500 c00 102 4 500 c00 102 4
  //   500 c00 102 4 500 c00 102 4 500 c00 102 4 500 c00 102 4 500 c00 102 4 500 c00 102 4 500 c00 102 4
  //   500 c00 102 4 500 c00 102 4 500 c00 102 4 500 c00 102 4 500 c00 102 4 500 c00 102 4 500 c00 102 4
  //   1008 0 102 4 1008 0 102 4 1008 0 102 4 1008 0 102 4 1008 0 102 4 1008 0 102 4 1008 0 102 4 1008 0
  //   102 4 1008 0 102 4 1008 0 102 4 1008 0 102 4 1008 0 102 4 1008 0 102 4 1008 0 102 4 1008 0 102 4
  //   1008 0 102 4 88 0 102 4 88 0 102 4 88 0 102 4 88 0 102 4 88 0 102 4 88 0 102 4 88 0 102 4 88 0 102 4
  //   88 0 102 4 88 0 102 4 88 0 102 4 88 0 102 4 88 0 102 4 88 0 102 4 88 0 102 4 88 0 102 4 4010 0 102 4
  //   4010 0 102 4 4010 0 102 4 4010 0 102 4 4010 0 102 4 4010 0 102 4 4010 0 102 4 4010 0 102 4 4010 0
  //   102 4 4010 0 102 4 4010 0 102 4 4010 0 102 4 4010 0 102 4 4010 0 102 4 4010 0 102 4 4010 0 102 8000
  //   0 0 0 8000 0 0 0 8000 0 0 0 8000 0 0 0 8000 0 0 0 8000 0 0 0 8000 0 0 0 8000 0 0 0 8000 0 0 0 8000 0
  //   0 0 8000 0 0 0 8000 0 0 0 8000 0 0 0 8000 0 0 0 8000 0 0 0 8000
endmodule

module InstructionRegister (
  input  [7:0] in_1,
  input  [7:0] in_2,
  input  in_3,
  input  in_4,
  input  in_5,
  input  in_6,
  output [7:0] out_7,
  output [7:0] out_8
);

  wire [7:0] multiplexer_1_out;

  LED led_1 (.in(out_8[7]));
  LED led_2 (.in(out_8[6]));
  LED led_3 (.in(out_8[5]));
  Multiplexer #(.width(8)) multiplexer_1 (.in0(in_1), .in1(in_2), .out(multiplexer_1_out), .sel(in_3));
  LED led_4 (.in(out_8[4]));
  LED led_5 (.in(out_8[3]));
  LED led_6 (.in(out_8[2]));
  LED led_7 (.in(out_8[1]));
  Register register_1 (.D(multiplexer_1_out), .en(1'b1), .clk(in_4), .Q(out_8), .clr(in_5));
  LED led_8 (.in(out_8[0]));
  assign out_7 = in_6 ? out_8 : 8'bz;  // Controlled_Buffer controlled_buffer_1
endmodule

module MemoryAddressRegister (
  input  [7:0] in_1,
  input  in_2,
  input  in_3,
  input  in_4,
  output [7:0] out_5
);

  LED led_1 (.in(out_5[7]));
  LED led_2 (.in(out_5[6]));
  LED led_3 (.in(out_5[5]));
  LED led_4 (.in(out_5[4]));
  LED led_5 (.in(out_5[3]));
  LED led_6 (.in(out_5[2]));
  Register register_1 (.D(in_1), .en(in_2), .clk(in_3), .Q(out_5), .clr(in_4));
  LED led_7 (.in(out_5[1]));
  LED led_8 (.in(out_5[0]));
endmodule

module RAM_256B (
  input  [7:0] in_1,
  input  in_2,
  input  in_3,
  input  CLK,
  input  [7:0] in_5,
  output [7:0] out_6,
  output [7:0] out_7
);

  wire [7:0] ram_1_dout;

  Hex_Digit_Display hex_digit_display_1 (.value(in_1[7:4]));  // open: dp
  Hex_Digit_Display hex_digit_display_2 (.value(in_1[3:0]));  // open: dp
  RAM #(.asyncread("true"), .clearpin("true"), .dataWidth(16)) ram_1 (
    .addr(in_1), .we(in_2), .oe(1'b1), .clk(CLK), .din({{8{1'b0}}, in_5}), .dout({out_7, ram_1_dout}));  // open: clr
  assign out_6 = in_3 ? ram_1_dout : 8'bz;  // Controlled_Buffer controlled_buffer_1
endmodule

module PC (
  input  CLR,
  input  STR,
  input  CE,
  input  CLK,
  input  [7:0] in_5,
  input  CO,
  output [7:0] out_7
);

  wire [7:0] counter_1_q;

  Counter counter_1 (.clr(CLR), .load(STR), .count(CE), .clk(CLK), .D(in_5), .Q(counter_1_q));  // open: up, carry
  LED led_1 (.in(counter_1_q[7]));
  LED led_2 (.in(counter_1_q[6]));
  LED led_3 (.in(counter_1_q[5]));
  LED led_4 (.in(counter_1_q[4]));
  LED led_5 (.in(counter_1_q[3]));
  LED led_6 (.in(counter_1_q[2]));
  LED led_7 (.in(counter_1_q[1]));
  LED led_8 (.in(counter_1_q[0]));
  assign out_7 = CO ? counter_1_q : 8'bz;  // Controlled_Buffer controlled_buffer_1
endmodule

module ALU (
  input  [3:0] in_1,
  input  [7:0] A,
  input  [7:0] B,
  input  in_4,
  input  in_5,
  input  in_6,
  output [7:0] out_7,
  output [3:0] out_8
);

  wire eightbitsadder_1_co, eightbitsadder_1_overflow, nor_1_out, or_2_out, or_3_out, or_4_out, or_5_out,
       or_6_out, or_7_out;
  wire [7:0] eightbitsadder_1_out_7, inverter_1_out_3, inverter_2_out_3, inverter_3_out_3, multiplexer_1_out,
       or_1_out, pla_1_out, shifters_1_out_3;

  PLA #(.in_width(4), .out_width(8), .\table ("0000 00000000 # ADD\n0001 00001000 # ADC\n0010 00001001 # SUB\n0011 00000010 # NOA\n0100 00000001 # NOB\n0101 00000100 # NOT\n0110 00010000 # OR\n0111 00010100 # NOR\n1000 00100000 # XOR\n1001 00100100 # XNOR\n1010 00010111 # AND\n1011 00010011 # NAND\n1100 01000000 # LSL\n1101 10000000 # LSR\n1110 11000000 # ASR")) pla_1 (
    .in(in_1), .out(pla_1_out));
  Inverter inverter_1 (.in_2(pla_1_out[1]), .in_1(A), .out_3(inverter_1_out_3));
  Inverter inverter_2 (.in_2(pla_1_out[0]), .in_1(B), .out_3(inverter_2_out_3));
  EightBitsAdder eightbitsadder_1 (
    .in_1(inverter_1_out_3), .in_2(inverter_2_out_3), .Ci(pla_1_out[3]), .in_3(pla_1_out[5]),
    .Overflow(eightbitsadder_1_overflow), .CO(eightbitsadder_1_co), .out_7(eightbitsadder_1_out_7));
  assign or_1_out = inverter_1_out_3 | inverter_2_out_3;  // OR_Gate or_1, 8 bits wide
  Multiplexer #(.width(8)) multiplexer_1 (
    .in0(eightbitsadder_1_out_7), .in1(or_1_out), .out(multiplexer_1_out), .sel(pla_1_out[4]));
  Shifters shifters_1 (.in_1(multiplexer_1_out), .in_2(pla_1_out[7:6]), .out_3(shifters_1_out_3));
  Inverter inverter_3 (.in_2(pla_1_out[2]), .in_1(shifters_1_out_3), .out_3(inverter_3_out_3));
  LED led_1 (.in(inverter_3_out_3[7]));
  LED led_2 (.in(inverter_3_out_3[6]));
  LED led_3 (.in(inverter_3_out_3[5]));
  LED led_4 (.in(inverter_3_out_3[4]));
  or or_2 (or_2_out, inverter_3_out_3[0], inverter_3_out_3[1]);
  or or_3 (or_3_out, or_2_out, or_4_out);
  or or_4 (or_4_out, inverter_3_out_3[2], inverter_3_out_3[3]);
  or or_5 (or_5_out, inverter_3_out_3[4], inverter_3_out_3[5]);
  or or_6 (or_6_out, or_5_out, or_7_out);
  or or_7 (or_7_out, inverter_3_out_3[6], inverter_3_out_3[7]);
  LED led_5 (.in(inverter_3_out_3[3]));
  LED led_6 (.in(inverter_3_out_3[2]));
  LED led_7 (.in(inverter_3_out_3[1]));
  LED led_8 (.in(inverter_3_out_3[0]));
  D_Flip_Flop d_ff_1 (.D(nor_1_out), .clk(in_5), .Q(out_8[0]), .reset(in_6));  // open: Qn, preset
  nor nor_1 (nor_1_out, or_3_out, or_6_out);
  D_Flip_Flop d_ff_2 (.D(eightbitsadder_1_co), .clk(in_5), .Q(out_8[1]), .reset(in_6));  // open: Qn, preset
  D_Flip_Flop d_ff_3 (.D(inverter_3_out_3[7]), .clk(in_5), .Q(out_8[2]), .reset(in_6));  // open: Qn, preset
  D_Flip_Flop d_ff_4 (.D(eightbitsadder_1_overflow), .clk(in_5), .Q(out_8[3]), .reset(in_6));  // open: Qn, preset
  assign out_7 = in_4 ? inverter_3_out_3 : 8'bz;  // Controlled_Buffer controlled_buffer_1
  LED led_9 (.in(out_8[0]));
  LED led_10 (.in(out_8[1]));
  LED led_11 (.in(out_8[2]));
  LED led_12 (.in(out_8[3]));
endmodule

module Register_A (
  input  [7:0] in_1,
  input  in_2,
  input  in_3,
  input  in_4,
  input  in_5,
  output [7:0] out_6,
  output [7:0] out_7
);

  LED led_1 (.in(out_7[7]));
  LED led_2 (.in(out_7[6]));
  LED led_3 (.in(out_7[5]));
  LED led_4 (.in(out_7[4]));
  LED led_5 (.in(out_7[3]));
  LED led_6 (.in(out_7[2]));
  Register register_1 (.D(in_1), .en(in_2), .clk(in_3), .Q(out_7), .clr(in_4));
  LED led_7 (.in(out_7[1]));
  LED led_8 (.in(out_7[0]));
  assign out_6 = in_5 ? out_7 : 8'bz;  // Controlled_Buffer controlled_buffer_1
endmodule

module Register_B (
  input  [7:0] in_1,
  input  in_2,
  input  in_3,
  input  in_4,
  input  in_5,
  output [7:0] out_6,
  output [7:0] out_7
);

  LED led_1 (.in(out_7[7]));
  LED led_2 (.in(out_7[6]));
  LED led_3 (.in(out_7[5]));
  LED led_4 (.in(out_7[4]));
  LED led_5 (.in(out_7[3]));
  LED led_6 (.in(out_7[2]));
  Register register_1 (.D(in_1), .en(in_2), .clk(in_3), .Q(out_7), .clr(in_4));
  LED led_7 (.in(out_7[1]));
  LED led_8 (.in(out_7[0]));
  assign out_6 = in_5 ? out_7 : 8'bz;  // Controlled_Buffer controlled_buffer_1
endmodule

module EightBitsAdder (
  input  [7:0] in_1,
  input  [7:0] in_2,
  input  in_3,
  input  Ci,
  output Overflow,
  output CO,
  output [7:0] out_7
);

  wire and_2_out, and_3_out, and_4_out, and_5_out, and_6_out, and_7_out, and_8_out, fulladder_1_out_4,
       fulladder_2_out_4, fulladder_3_out_4, fulladder_4_out_4, fulladder_5_out_4, fulladder_6_out_4,
       fulladder_7_out_4, fulladder_8_out_4, not_1_out;

  FullAdder fulladder_1 (.in_3(and_2_out), .in_1(in_1[7]), .in_2(in_2[7]), .out_5(out_7[7]), .out_4(fulladder_1_out_4));
  FullAdder fulladder_2 (.in_3(and_3_out), .in_1(in_1[6]), .in_2(in_2[6]), .out_5(out_7[6]), .out_4(fulladder_2_out_4));
  FullAdder fulladder_3 (.in_3(and_4_out), .in_1(in_1[5]), .in_2(in_2[5]), .out_5(out_7[5]), .out_4(fulladder_3_out_4));
  FullAdder fulladder_4 (.in_3(and_5_out), .in_1(in_1[4]), .in_2(in_2[4]), .out_5(out_7[4]), .out_4(fulladder_4_out_4));
  FullAdder fulladder_5 (.in_3(and_6_out), .in_1(in_1[3]), .in_2(in_2[3]), .out_5(out_7[3]), .out_4(fulladder_5_out_4));
  FullAdder fulladder_6 (.in_3(and_7_out), .in_1(in_1[2]), .in_2(in_2[2]), .out_5(out_7[2]), .out_4(fulladder_6_out_4));
  FullAdder fulladder_7 (.in_3(and_8_out), .in_1(in_1[1]), .in_2(in_2[1]), .out_5(out_7[1]), .out_4(fulladder_7_out_4));
  FullAdder fulladder_8 (.in_3(Ci), .in_1(in_1[0]), .in_2(in_2[0]), .out_5(out_7[0]), .out_4(fulladder_8_out_4));
  not not_1 (not_1_out, in_3);
  xor xor_1 (Overflow, fulladder_2_out_4, fulladder_1_out_4);
  and and_1 (CO, not_1_out, fulladder_1_out_4);
  and and_2 (and_2_out, not_1_out, fulladder_2_out_4);
  and and_3 (and_3_out, not_1_out, fulladder_3_out_4);
  and and_4 (and_4_out, not_1_out, fulladder_4_out_4);
  and and_5 (and_5_out, not_1_out, fulladder_5_out_4);
  and and_6 (and_6_out, not_1_out, fulladder_6_out_4);
  and and_7 (and_7_out, not_1_out, fulladder_7_out_4);
  and and_8 (and_8_out, not_1_out, fulladder_8_out_4);
endmodule

module FullAdder (
  input  in_1,
  input  in_2,
  input  in_3,
  output out_4,
  output out_5
);

  wire and_1_out, and_2_out, xor_1_out;

  and and_1 (and_1_out, in_1, in_2);
  xor xor_1 (xor_1_out, in_1, in_2);
  and and_2 (and_2_out, xor_1_out, in_3);
  xor xor_2 (out_5, xor_1_out, in_3);
  or or_1 (out_4, and_1_out, and_2_out);
endmodule

module Inverter (
  input  [7:0] in_1,
  input  in_2,
  output [7:0] out_3
);

  wire [7:0] pull_resistor_1_node;

  Pull_Resistor pull_resistor_1 (.node(pull_resistor_1_node));
  assign pull_resistor_1_node = in_2 ? {8{1'b1}} : 8'bz;  // Controlled_Buffer controlled_buffer_1
  assign out_3 = in_1 ^ pull_resistor_1_node;  // XOR_Gate xor_1, 8 bits wide
endmodule

module Shifters (
  input  [7:0] in_1,
  input  [1:0] in_2,
  output [7:0] out_3
);

  wire [7:0] shifter_1_out, shifter_2_out, shifter_3_out;

  Shifter shifter_1 (.in(in_1), .\dist (3'b001), .out(shifter_1_out));
  Shifter #(.shift("lr")) shifter_2 (.in(in_1), .\dist (3'b001), .out(shifter_2_out));
  Shifter #(.shift("ar")) shifter_3 (.in(in_1), .\dist (3'b001), .out(shifter_3_out));
  Multiplexer #(.select(2), .width(8)) multiplexer_1 (
    .in0(in_1), .in1(shifter_1_out), .in2(shifter_2_out), .in3(shifter_3_out), .out(out_3), .sel(in_2));
endmodule

module OutReg (
  input  [7:0] in_1,
  input  in_2,
  input  in_3,
  input  in_4
);

  wire [7:0] register_1_q;

  Register register_1 (.D(in_1), .en(in_2), .clk(in_3), .Q(register_1_q), .clr(in_4));
  LED led_1 (.in(register_1_q[7]));
  LED led_2 (.in(register_1_q[6]));
  Hex_Digit_Display hex_digit_display_1 ();  // open: value, dp
  Hex_Digit_Display hex_digit_display_2 ();  // open: value, dp
  // Binary_to_BCD_converter #(.binvalue(8)) binary_to_bcd_converter_1: pin names not known; wires that end beside it: register_1_q
  LED led_3 (.in(register_1_q[5]));
  LED led_4 (.in(register_1_q[4]));
  LED led_5 (.in(register_1_q[3]));
  LED led_6 (.in(register_1_q[2]));
  Hex_Digit_Display hex_digit_display_3 ();  // open: value, dp
  Hex_Digit_Display hex_digit_display_4 (.value(register_1_q[7:4]));  // open: dp
  Hex_Digit_Display hex_digit_display_5 (.value(register_1_q[3:0]));  // open: dp
  LED led_7 (.in(register_1_q[1]));
  LED led_8 (.in(register_1_q[0]));
endmodule

module HardwareStack (
  input  RST,
  input  CLK,
  input  Push,
  input  Pop,
  input  [7:0] in_5,
  output [7:0] out_6
);

  wire multiplexer_1_out, not_1_out, not_2_out, not_3_out, or_1_out;
  wire [7:0] counter_1_q, ram_1_dout, register_1_q;

  or or_1 (or_1_out, Push, Pop);
  Counter counter_1 (
    .clr(RST), .up(not_1_out), .count(or_1_out), .clk(multiplexer_1_out), .Q(counter_1_q));  // open: load, D, carry
  not not_1 (not_1_out, Pop);
  not not_2 (not_2_out, CLK);
  Multiplexer multiplexer_1 (.in0(not_2_out), .in1(CLK), .out(multiplexer_1_out), .sel(or_1_out));
  not not_3 (not_3_out, CLK);
  Register register_1 (.D(in_5), .clk(CLK), .Q(register_1_q), .clr(RST));  // open: en
  Hex_Digit_Display hex_digit_display_1 (.value(counter_1_q[3:0]));  // open: dp
  RAM #(.clearpin("true")) ram_1 (
    .addr(counter_1_q), .we(Push), .oe(Pop), .clk(not_3_out), .din(register_1_q), .dout(ram_1_dout), .clr(RST));
  Hex_Digit_Display hex_digit_display_2 (.value(counter_1_q[7:4]));  // open: dp
  assign out_6 = Pop ? ram_1_dout : 8'bz;  // Controlled_Buffer controlled_buffer_1
endmodule
